// Logisim project FSM.circ as structural Verilog: 4 circuits, main circuit main
module main (
  input  Input,
  input  Reset
);

  wire A_q, B_q, C_q, Clock_out, d0_1_d0, d1_1_d1, d2_1_d2, nor_1_out;

  Clock Clock (.out(Clock_out));
  D_Flip_Flop A (.D(d0_1_d0), .clk(Clock_out), .Q(A_q), .reset(Reset));  // open: Qn, preset
  D0 d0_1 (.Q0(A_q), .Q1(B_q), .Q2(C_q), .I(Input), .D0(d0_1_d0));
  D_Flip_Flop B (.D(d1_1_d1), .clk(Clock_out), .Q(B_q), .reset(Reset));  // open: Qn, preset
  D1 d1_1 (.Q0(A_q), .Q1(B_q), .Q2(C_q), .I(Input), .D1(d1_1_d1));
  D_Flip_Flop C (.D(d2_1_d2), .clk(Clock_out), .Q(C_q), .reset(Reset));  // open: Qn, preset
  D2 d2_1 (.Q0(A_q), .Q1(B_q), .Q2(C_q), .I(Input), .D2(d2_1_d2));
  nor nor_1 (nor_1_out, A_q, B_q, C_q);
  // Probe on nor_1_out

  // Notes on the sheet:
  //   Reset for D Flip Flops
endmodule

module D0 (
  input  Q0,
  input  Q1,
  input  Q2,
  input  I,
  output D0
);

  wire and_1_out, and_2_out, not_1_out, not_2_out, not_3_out, not_4_out;

  not not_1 (not_1_out, Q0);
  not not_2 (not_2_out, Q1);
  not not_3 (not_3_out, Q2);
  not not_4 (not_4_out, I);
  and and_1 (and_1_out, not_1_out, Q1, not_3_out, not_4_out);
  and and_2 (and_2_out, Q0, not_2_out, not_3_out, I);
  or or_1 (D0, and_1_out, and_2_out);
endmodule

module D1 (
  input  Q0,
  input  Q1,
  input  Q2,
  input  I,
  output D1
);

  wire and_1_out, and_2_out, not_1_out, not_2_out, not_3_out, xor_1_out;

  not not_1 (not_1_out, Q0);
  not not_2 (not_2_out, Q1);
  and and_1 (and_1_out, not_1_out, I, Q2);
  not not_3 (not_3_out, I);
  xor xor_1 (xor_1_out, Q2, Q0);
  or or_1 (D1, and_1_out, and_2_out);
  and and_2 (and_2_out, not_2_out, not_3_out, xor_1_out);
endmodule

module D2 (
  input  Q0,
  input  Q1,
  input  Q2,
  input  I,
  output D2
);

  wire and_1_out, and_2_out, and_3_out, not_1_out, not_2_out, not_3_out, not_4_out;

  not not_1 (not_1_out, Q0);
  not not_2 (not_2_out, Q1);
  not not_3 (not_3_out, Q2);
  not not_4 (not_4_out, I);
  and and_1 (and_1_out, not_1_out, not_2_out, I);
  and and_2 (and_2_out, not_1_out, Q1, Q2, not_4_out);
  and and_3 (and_3_out, Q0, not_2_out, not_3_out, not_4_out);
  or or_1 (D2, and_1_out, and_2_out, and_3_out);
endmodule
