// Logisim project Four_Bits_Add_Sub.circ as structural Verilog: 2 circuits, main circuit Add_Sub_4Bits
module Add_1Bit (
  input  Cin,
  input  A,
  input  B,
  output Sum,
  output Cout
);

  wire and_1_out, and_2_out, xor_1_out;

  xor xor_1 (xor_1_out, A, B);
  xor xor_2 (Sum, Cin, xor_1_out);
  and and_1 (and_1_out, Cin, xor_1_out);
  and and_2 (and_2_out, A, B);
  or or_1 (Cout, and_1_out, and_2_out);

  // Notes on the sheet:
  //   Namdar Kabolinejad, 260893536
  //   MAKE SURE THAT YOU OPENED THIS PROJECT IN "LOGISIM-EVOLUTION"
endmodule

module Add_Sub_4Bits (
  input  [3:0] A,
  input  [3:0] B,
  input  Add_Sub,
  output [3:0] R,
  output Zero,
  output Overflow
);

  wire add_1bit_1_cout, add_1bit_2_cout, add_1bit_3_cout, or_1_out, or_2_out, or_3_out, or_4_out, xor_1_out,
       xor_2_out, xor_3_out, xor_4_out, xor_5_out;

  // Probe on A
  // Probe on B
  xor xor_1 (xor_1_out, B[0], Add_Sub);
  xor xor_2 (xor_2_out, B[1], Add_Sub);
  xor xor_3 (xor_3_out, B[2], Add_Sub);
  xor xor_4 (xor_4_out, B[3], Add_Sub);
  // Probe on R
  Add_1Bit add_1bit_1 (.Sum(R[0]), .A(A[0]), .B(xor_1_out), .Cout(add_1bit_1_cout), .Cin(Add_Sub));
  Add_1Bit add_1bit_2 (.Sum(R[1]), .A(A[1]), .B(xor_2_out), .Cout(add_1bit_2_cout), .Cin(add_1bit_1_cout));
  not not_1 (Zero, or_1_out);
  Add_1Bit add_1bit_3 (.Sum(R[2]), .A(A[2]), .B(xor_3_out), .Cout(add_1bit_3_cout), .Cin(add_1bit_2_cout));
  Add_1Bit add_1bit_4 (.Sum(R[3]), .A(A[3]), .B(xor_4_out), .Cout(Overflow), .Cin(add_1bit_3_cout));
  or or_1 (or_1_out, R[0], or_2_out);
  or or_2 (or_2_out, or_3_out, or_4_out);
  or or_3 (or_3_out, R[1], R[2]);
  xor xor_5 (xor_5_out, add_1bit_3_cout, Overflow);
  or or_4 (or_4_out, R[3], xor_5_out);

  // Notes on the sheet:
  //   Namdar Kabolinejad, 260893536
  //   MAKE SURE THAT YOU OPEN THIS PROJECT IN "LOGISIM-EVOLUTION"
endmodule
