// Logisim project RAM_16_Nibbles_Read_Write.circ as structural Verilog: 4 circuits, main circuit Nibble
// Clk
module RAM_16_Nibbles (
  input  Read_Write,
  input  [3:0] Address,
  input  [3:0] Data,
  output [3:0] RAM_OUT
);

  wire Clk_out, multiplexor_1_e, multiplexor_1_e0, multiplexor_1_e1, multiplexor_1_e2, multiplexor_1_e3,
       multiplexor_1_e4, multiplexor_1_e6, multiplexor_1_e7, multiplexor_1_e8, multiplexor_1_e9,
       multiplexor_1_e10, multiplexor_1_e11, multiplexor_1_e12, multiplexor_1_e13, multiplexor_1_e14,
       multiplexor_1_e15;
  wire [3:0] Bit_Mask_out_3, mask_1_out_3, mask_2_out_3, mask_3_out_3, mask_4_out_3, mask_5_out_3,
       mask_6_out_3, mask_7_out_3, mask_8_out_3, mask_9_out_3, mask_10_out_3, mask_11_out_3, mask_12_out_3,
       mask_13_out_3, mask_14_out_3, mask_15_out_3, multiplexor_1_n0, multiplexor_1_n1, multiplexor_1_n2,
       multiplexor_1_n3, multiplexor_1_n4, multiplexor_1_n5, multiplexor_1_n6, multiplexor_1_n7,
       multiplexor_1_n8, multiplexor_1_n9, multiplexor_1_n10, multiplexor_1_n11, multiplexor_1_n12,
       multiplexor_1_n13, multiplexor_1_n14, multiplexor_1_n15, nibble_1_nibble_out, nibble_2_nibble_out,
       nibble_3_nibble_out, nibble_4_nibble_out, nibble_5_nibble_out, nibble_6_nibble_out,
       nibble_7_nibble_out, nibble_8_nibble_out, nibble_9_nibble_out, nibble_10_nibble_out,
       nibble_11_nibble_out, nibble_12_nibble_out, nibble_13_nibble_out, nibble_14_nibble_out,
       nibble_15_nibble_out, Nibbles_nibble_out;

  // Probe on Address
  // Probe on Data
  Multiplexor multiplexor_1 (
    .A3(Address[3]), .A2(Address[2]), .A1(Address[1]), .A0(Address[0]), .D3(Data[3]), .D2(Data[2]),
    .D1(Data[1]), .D0(Data[0]), .E0(multiplexor_1_e0), .E1(multiplexor_1_e1), .E2(multiplexor_1_e2),
    .E3(multiplexor_1_e3), .E4(multiplexor_1_e4), .E(multiplexor_1_e), .E6(multiplexor_1_e6),
    .E7(multiplexor_1_e7), .E8(multiplexor_1_e8), .E9(multiplexor_1_e9), .E10(multiplexor_1_e10),
    .E11(multiplexor_1_e11), .E12(multiplexor_1_e12), .E13(multiplexor_1_e13), .E14(multiplexor_1_e14),
    .E15(multiplexor_1_e15), .N0(multiplexor_1_n0), .N1(multiplexor_1_n1), .N2(multiplexor_1_n2),
    .N3(multiplexor_1_n3), .N4(multiplexor_1_n4), .N5(multiplexor_1_n5), .N6(multiplexor_1_n6),
    .N7(multiplexor_1_n7), .N8(multiplexor_1_n8), .N9(multiplexor_1_n9), .N10(multiplexor_1_n10),
    .N11(multiplexor_1_n11), .N12(multiplexor_1_n12), .N13(multiplexor_1_n13), .N14(multiplexor_1_n14),
    .N15(multiplexor_1_n15));
  Clock Clk (.out(Clk_out));
  Nibble Nibbles (
    .Enable(multiplexor_1_e0), .Read_Write(Read_Write), .Data(multiplexor_1_n0), .Clk(Clk_out),
    .Nibble_Out(Nibbles_nibble_out));
  Nibble nibble_1 (
    .Enable(multiplexor_1_e1), .Read_Write(Read_Write), .Data(multiplexor_1_n1), .Clk(Clk_out),
    .Nibble_Out(nibble_1_nibble_out));
  Nibble nibble_2 (
    .Enable(multiplexor_1_e2), .Read_Write(Read_Write), .Data(multiplexor_1_n2), .Clk(Clk_out),
    .Nibble_Out(nibble_2_nibble_out));
  Nibble nibble_3 (
    .Enable(multiplexor_1_e3), .Read_Write(Read_Write), .Data(multiplexor_1_n3), .Clk(Clk_out),
    .Nibble_Out(nibble_3_nibble_out));
  Nibble nibble_4 (
    .Enable(multiplexor_1_e4), .Read_Write(Read_Write), .Data(multiplexor_1_n4), .Clk(Clk_out),
    .Nibble_Out(nibble_4_nibble_out));
  Nibble nibble_5 (
    .Enable(multiplexor_1_e), .Read_Write(Read_Write), .Data(multiplexor_1_n5), .Clk(Clk_out),
    .Nibble_Out(nibble_5_nibble_out));
  Nibble nibble_6 (
    .Enable(multiplexor_1_e6), .Read_Write(Read_Write), .Data(multiplexor_1_n6), .Clk(Clk_out),
    .Nibble_Out(nibble_6_nibble_out));
  Nibble nibble_7 (
    .Enable(multiplexor_1_e7), .Read_Write(Read_Write), .Data(multiplexor_1_n7), .Clk(Clk_out),
    .Nibble_Out(nibble_7_nibble_out));
  Nibble nibble_8 (
    .Enable(multiplexor_1_e8), .Read_Write(Read_Write), .Data(multiplexor_1_n8), .Clk(Clk_out),
    .Nibble_Out(nibble_8_nibble_out));
  Nibble nibble_9 (
    .Enable(multiplexor_1_e9), .Read_Write(Read_Write), .Data(multiplexor_1_n9), .Clk(Clk_out),
    .Nibble_Out(nibble_9_nibble_out));
  Nibble nibble_10 (
    .Enable(multiplexor_1_e10), .Read_Write(Read_Write), .Data(multiplexor_1_n10), .Clk(Clk_out),
    .Nibble_Out(nibble_10_nibble_out));
  Nibble nibble_11 (
    .Enable(multiplexor_1_e11), .Read_Write(Read_Write), .Data(multiplexor_1_n11), .Clk(Clk_out),
    .Nibble_Out(nibble_11_nibble_out));
  Nibble nibble_12 (
    .Enable(multiplexor_1_e12), .Read_Write(Read_Write), .Data(multiplexor_1_n12), .Clk(Clk_out),
    .Nibble_Out(nibble_12_nibble_out));
  Nibble nibble_13 (
    .Enable(multiplexor_1_e13), .Read_Write(Read_Write), .Data(multiplexor_1_n13), .Clk(Clk_out),
    .Nibble_Out(nibble_13_nibble_out));
  Nibble nibble_14 (
    .Enable(multiplexor_1_e14), .Read_Write(Read_Write), .Data(multiplexor_1_n14), .Clk(Clk_out),
    .Nibble_Out(nibble_14_nibble_out));
  Nibble nibble_15 (
    .Enable(multiplexor_1_e15), .Read_Write(Read_Write), .Data(multiplexor_1_n15), .Clk(Clk_out),
    .Nibble_Out(nibble_15_nibble_out));
  Mask Bit_Mask (.Enable(multiplexor_1_e0), .Nibble_Out(Nibbles_nibble_out), .out_3(Bit_Mask_out_3));
  Mask mask_1 (.Enable(multiplexor_1_e1), .Nibble_Out(nibble_1_nibble_out), .out_3(mask_1_out_3));
  Mask mask_2 (.Enable(multiplexor_1_e2), .Nibble_Out(nibble_2_nibble_out), .out_3(mask_2_out_3));
  Mask mask_3 (.Enable(multiplexor_1_e3), .Nibble_Out(nibble_3_nibble_out), .out_3(mask_3_out_3));
  Mask mask_4 (.Enable(multiplexor_1_e4), .Nibble_Out(nibble_4_nibble_out), .out_3(mask_4_out_3));
  Mask mask_5 (.Enable(multiplexor_1_e), .Nibble_Out(nibble_5_nibble_out), .out_3(mask_5_out_3));
  Mask mask_6 (.Enable(multiplexor_1_e6), .Nibble_Out(nibble_6_nibble_out), .out_3(mask_6_out_3));
  Mask mask_7 (.Enable(multiplexor_1_e7), .Nibble_Out(nibble_7_nibble_out), .out_3(mask_7_out_3));
  Mask mask_8 (.Enable(multiplexor_1_e8), .Nibble_Out(nibble_8_nibble_out), .out_3(mask_8_out_3));
  Mask mask_9 (.Enable(multiplexor_1_e9), .Nibble_Out(nibble_9_nibble_out), .out_3(mask_9_out_3));
  Mask mask_10 (.Enable(multiplexor_1_e10), .Nibble_Out(nibble_10_nibble_out), .out_3(mask_10_out_3));
  Mask mask_11 (.Enable(multiplexor_1_e11), .Nibble_Out(nibble_11_nibble_out), .out_3(mask_11_out_3));
  Mask mask_12 (.Enable(multiplexor_1_e12), .Nibble_Out(nibble_12_nibble_out), .out_3(mask_12_out_3));
  Mask mask_13 (.Enable(multiplexor_1_e13), .Nibble_Out(nibble_13_nibble_out), .out_3(mask_13_out_3));
  Mask mask_14 (.Enable(multiplexor_1_e14), .Nibble_Out(nibble_14_nibble_out), .out_3(mask_14_out_3));
  Mask mask_15 (.Enable(multiplexor_1_e15), .Nibble_Out(nibble_15_nibble_out), .out_3(mask_15_out_3));
  // Probe on RAM_OUT
  assign RAM_OUT = Bit_Mask_out_3 | mask_1_out_3 | mask_2_out_3 | mask_3_out_3 | mask_4_out_3 | mask_5_out_3 | mask_6_out_3 | mask_7_out_3 | mask_8_out_3 | mask_9_out_3 | mask_10_out_3 | mask_11_out_3 | mask_12_out_3 | mask_13_out_3 | mask_14_out_3 | mask_15_out_3;  // OR_Gate or_1, 4 bits wide

  // Notes on the sheet:
  //   When Read_Write = 0 performs read, otherwise performs write
  //   MAKE SURE THAT YOU OPEN THIS PROJECT IN "LOGISIM-EVOLUTION"
endmodule

module Nibble (
  input  Enable,
  input  Read_Write,
  input  [3:0] Data,
  input  Clk,
  output [3:0] Nibble_Out
);

  wire and_1_out, and_2_out, and_3_out, and_4_out, and_5_out, and_6_out;

  // Probe on Data
  D_Flip_Flop d_ff_1 (.D(and_1_out), .clk(and_2_out), .Q(Nibble_Out[0]));  // open: Qn, preset, reset
  and and_1 (and_1_out, Read_Write, Data[0]);
  and and_2 (and_2_out, Clk, and_4_out);
  and and_3 (and_3_out, Read_Write, Data[1]);
  and and_4 (and_4_out, Read_Write, Enable);
  D_Flip_Flop d_ff_2 (.D(and_3_out), .clk(and_2_out), .Q(Nibble_Out[1]));  // open: Qn, preset, reset
  and and_5 (and_5_out, Read_Write, Data[2]);
  D_Flip_Flop d_ff_3 (.D(and_5_out), .clk(and_2_out), .Q(Nibble_Out[2]));  // open: Qn, preset, reset
  D_Flip_Flop d_ff_4 (.D(and_6_out), .clk(and_2_out), .Q(Nibble_Out[3]));  // open: Qn, preset, reset
  and and_6 (and_6_out, Read_Write, Data[3]);
  // Probe on Nibble_Out

  // Notes on the sheet:
  //   When Read_Write = 0 performs read, otherwise performs write
  //   MAKE SURE THAT YOU OPEN THIS PROJECT IN "LOGISIM-EVOLUTION"
  //   The data value is passed throuth only when they are both 1, otherwise thw nibble will hold their old value.
endmodule

// MUX
module Multiplexor (
  input  A3,
  input  A2,
  input  A1,
  input  A0,
  input  D3,
  input  D2,
  input  D1,
  input  D0,
  output [3:0] N0,
  output E0,
  output [3:0] N1,
  output E1,
  output [3:0] N2,
  output E2,
  output [3:0] N3,
  output E3,
  output [3:0] N4,
  output E4,
  output [3:0] N5,
  output E,
  output [3:0] N6,
  output E6,
  output [3:0] N7,
  output E7,
  output [3:0] N8,
  output E8,
  output [3:0] N9,
  output E9,
  output [3:0] N10,
  output E10,
  output [3:0] N11,
  output E11,
  output [3:0] N12,
  output E12,
  output [3:0] N13,
  output E13,
  output [3:0] N14,
  output E14,
  output [3:0] N15,
  output E15
);

  wire not_1_out, not_2_out, not_3_out, not_4_out;

  not not_1 (not_1_out, A3);
  not not_2 (not_2_out, A2);
  not not_3 (not_3_out, A1);
  not not_4 (not_4_out, A0);
  and and_1 (E0, not_1_out, not_2_out, not_3_out, not_4_out);
  and and_2 (E1, not_1_out, not_2_out, not_3_out, A0);
  and and_3 (E2, not_1_out, not_2_out, A1, not_4_out);
  and and_4 (E3, not_1_out, not_2_out, A1, A0);
  and and_5 (E4, not_1_out, A2, not_3_out, not_4_out);
  and and_6 (E, not_1_out, A2, not_3_out, A0);
  and and_7 (E6, not_1_out, A2, A1, not_4_out);
  and and_8 (E7, not_1_out, A2, A1, A0);
  and and_9 (E8, A3, not_2_out, not_3_out, not_4_out);
  and and_10 (E9, A3, not_2_out, not_3_out, A0);
  and and_11 (E10, A3, not_2_out, A1, not_4_out);
  and and_12 (E11, A3, not_2_out, A1, A0);
  and and_13 (E12, A3, A2, not_3_out, not_4_out);
  and and_14 (E13, A3, A2, not_3_out, A0);
  and and_15 (E14, A3, A2, A1, not_4_out);
  and and_16 (E15, A0, A1, A2, A3);
  and and_17 (N0[0], D0, E0);
  and and_18 (N0[1], D1, E0);
  and and_19 (N0[2], D2, E0);
  and and_20 (N0[3], D3, E0);
  and and_21 (N1[0], D0, E1);
  and and_22 (N1[1], D1, E1);
  and and_23 (N1[2], D2, E1);
  and and_24 (N1[3], D3, E1);
  and and_25 (N2[0], D0, E2);
  and and_26 (N2[1], D1, E2);
  and and_27 (N2[2], D2, E2);
  and and_28 (N2[3], D3, E2);
  and and_29 (N3[0], D0, E3);
  and and_30 (N3[1], D1, E3);
  and and_31 (N3[2], D2, E3);
  and and_32 (N3[3], D3, E3);
  and and_33 (N4[0], D0, E4);
  and and_34 (N4[1], D1, E4);
  and and_35 (N4[2], D2, E4);
  and and_36 (N4[3], D3, E4);
  and and_37 (N5[0], D0, E);
  and and_38 (N5[1], D1, E);
  and and_39 (N5[2], D2, E);
  and and_40 (N5[3], D3, E);
  and and_41 (N6[0], D0, E6);
  and and_42 (N6[1], D1, E6);
  and and_43 (N6[2], D2, E6);
  and and_44 (N6[3], D3, E6);
  and and_45 (N7[0], D0, E7);
  and and_46 (N7[1], D1, E7);
  and and_47 (N7[2], D2, E7);
  and and_48 (N7[3], D3, E7);
  and and_49 (N8[0], D0, E8);
  and and_50 (N8[1], D1, E8);
  and and_51 (N8[2], D2, E8);
  and and_52 (N8[3], D3, E8);
  and and_53 (N9[0], D0, E9);
  and and_54 (N9[1], D1, E9);
  and and_55 (N9[2], D2, E9);
  and and_56 (N9[3], D3, E9);
  and and_57 (N10[0], D0, E10);
  and and_58 (N10[1], D1, E10);
  and and_59 (N10[2], D2, E10);
  and and_60 (N10[3], D3, E10);
  and and_61 (N11[0], D0, E11);
  and and_62 (N11[1], D1, E11);
  and and_63 (N11[2], D2, E11);
  and and_64 (N11[3], D3, E11);
  and and_65 (N12[0], D0, E12);
  and and_66 (N12[1], D1, E12);
  and and_67 (N12[2], D2, E12);
  and and_68 (N12[3], D3, E12);
  and and_69 (N13[0], D0, E13);
  and and_70 (N13[1], D1, E13);
  and and_71 (N13[2], D2, E13);
  and and_72 (N13[3], D3, E13);
  and and_73 (N14[0], D0, E14);
  and and_74 (N14[1], D1, E14);
  and and_75 (N14[2], D2, E14);
  and and_76 (N14[3], D3, E14);
  and and_77 (N15[0], D0, E15);
  and and_78 (N15[1], D1, E15);
  and and_79 (N15[2], D2, E15);
  and and_80 (N15[3], D3, E15);

  // Notes on the sheet:
  //   Address
  //   Enable Bit
  //   Data
endmodule

module Mask (
  input  Enable,
  input  [3:0] Nibble_Out,
  output [3:0] out_3
);

  and and_1 (out_3[0], Nibble_Out[0], Enable);
  and and_2 (out_3[1], Nibble_Out[1], Enable);
  and and_3 (out_3[2], Nibble_Out[2], Enable);
  and and_4 (out_3[3], Nibble_Out[3], Enable);
endmodule
